// Logisim project Ashikur rahaman.circ as structural Verilog: 16 circuits, main circuit main
module main (
  input  CLEAR,
  output [3:0] HIGH,
  output [3:0] LOW,
  output out_4,
  output out_5,
  output out_6,
  output out_7,
  output out_8,
  output out_9,
  output out_10,
  output out_11
);

  wire CLOCK_out, controlled_buffer_1_out, controlled_buffer_6_out, controller_cp, controller_ea,
       controller_ep, controller_eu, controller_hlt, controller_nce, controller_nel, controller_nla,
       controller_nlb, controller_nll, controller_nlm, controller_nlo, controller_su, not_1_out, not_2_out,
       not_3_out, not_4_out, not_5_out, not_6_out, not_7_out, not_8_out;
  wire [3:0] _1607098_out0, _1607098_out4, MAR_4_bit__1607098_out0, PC_1607098_c0;
  wire [7:0] _1607032_2_output, _1607032_3_out0, _1607032_out0, bit_extender_1_out, xor_1_out;

  not not_1 (not_1_out, controller_nlm);
  assign controlled_buffer_1_out = controller_cp ? controlled_buffer_6_out : 1'bz;  // Controlled_Buffer controlled_buffer_1
  MAR_4_bit__1607098 MAR_4_bit__1607098 (
    .CP(controlled_buffer_6_out), .CL(CLEAR), .Load(not_1_out), .In0(LOW[0]), .In1(LOW[1]), .In2(LOW[2]),
    .In3(LOW[3]), .Out0(MAR_4_bit__1607098_out0[0]), .Out1(MAR_4_bit__1607098_out0[1]),
    .Out2(MAR_4_bit__1607098_out0[2]), .Out3(MAR_4_bit__1607098_out0[3]));
  not not_2 (not_2_out, controller_nce);
  not not_3 (not_3_out, controller_nll);
  program_counter_1607098___synchronous PC_1607098 (
    .Clock(controlled_buffer_1_out), .Clear(CLEAR), .C3(PC_1607098_c0[3]), .C2(PC_1607098_c0[2]),
    .C1(PC_1607098_c0[1]), .C0(PC_1607098_c0[0]));
  Instruction_Registe_1607098 _1607098 (
    .Load(not_3_out), .Clock(controlled_buffer_6_out), .Clear(CLEAR), .In7(HIGH[3]), .In6(HIGH[2]),
    .In5(HIGH[1]), .In4(HIGH[0]), .In3(LOW[3]), .In2(LOW[2]), .In1(LOW[1]), .In0(LOW[0]),
    .Out7(_1607098_out4[3]), .Out6(_1607098_out4[2]), .Out5(_1607098_out4[1]), .Out4(_1607098_out4[0]),
    .Out3(_1607098_out0[3]), .Out2(_1607098_out0[2]), .Out1(_1607098_out0[1]), .Out0(_1607098_out0[0]));
  controller_1607032_1607098 controller (
    .CLK(controlled_buffer_6_out), .Clear(CLEAR), .Cp(controller_cp), .Ep(controller_ep),
    .i7(_1607098_out4[3]), .i6(_1607098_out4[2]), .i5(_1607098_out4[1]), .i4(_1607098_out4[0]),
    .HLT(controller_hlt), .nLm(controller_nlm), .nCE(controller_nce), .nEl(controller_nel),
    .nLa(controller_nla), .Ea(controller_ea), .Su(controller_su), .Eu(controller_eu), .nLb(controller_nlb),
    .nLo(controller_nlo), .nLl(controller_nll));
  assign LOW = controller_ep ? PC_1607098_c0 : 4'bz;  // Controlled_Buffer controlled_buffer_2
  RAM #(.addrWidth(4)) ram_1 (
    .addr(MAR_4_bit__1607098_out0), .data({HIGH, LOW}), .ld(not_2_out));  // open: sel, clk, clr
  not not_4 (not_4_out, controller_nel);
  assign LOW = not_4_out ? _1607098_out0 : 4'bz;  // Controlled_Buffer controlled_buffer_3
  not not_5 (not_5_out, controller_nla);
  assign {HIGH, LOW} = controller_ea ? _1607032_out0 : 8'bz;  // Controlled_Buffer controlled_buffer_4
  not not_6 (not_6_out, controller_nlb);
  not not_7 (not_7_out, controller_nlo);
  A_Register_1607032 _1607032 (
    .Load(not_5_out), .Clock(controlled_buffer_6_out), .Clear(CLEAR), .In7(HIGH[3]), .In6(HIGH[2]),
    .In5(HIGH[1]), .In4(HIGH[0]), .In3(LOW[3]), .In2(LOW[2]), .In1(LOW[1]), .In0(LOW[0]),
    .Out7(_1607032_out0[7]), .Out6(_1607032_out0[6]), .Out5(_1607032_out0[5]), .Out4(_1607032_out0[4]),
    .Out3(_1607032_out0[3]), .Out2(_1607032_out0[2]), .Out1(_1607032_out0[1]), .Out0(_1607032_out0[0]));
  Adder_subtractor_1607032 _1607032_2 (
    .A(_1607032_out0), .B(xor_1_out), .Cin(controller_su), .Output(_1607032_2_output));  // open: Cout
  B_Register_1607032 _1607032_3 (
    .Load(not_6_out), .Clock(controlled_buffer_6_out), .Clear(CLEAR), .In7(HIGH[3]), .In6(HIGH[2]),
    .In5(HIGH[1]), .In4(HIGH[0]), .In3(LOW[3]), .In2(LOW[2]), .In1(LOW[1]), .In0(LOW[0]),
    .Out7(_1607032_3_out0[7]), .Out6(_1607032_3_out0[6]), .Out5(_1607032_3_out0[5]),
    .Out4(_1607032_3_out0[4]), .Out3(_1607032_3_out0[3]), .Out2(_1607032_3_out0[2]),
    .Out1(_1607032_3_out0[1]), .Out0(_1607032_3_out0[0]));
  Output_Register_1607032 _1607032_4 (
    .Load(not_7_out), .Clock(controlled_buffer_6_out), .Clear(CLEAR), .In7(HIGH[3]), .In6(HIGH[2]),
    .In5(HIGH[1]), .In4(HIGH[0]), .In3(LOW[3]), .In2(LOW[2]), .In1(LOW[1]), .In0(LOW[0]),
    .out_12({out_11, out_10, out_9, out_8, out_7, out_6, out_5, out_4}));
  assign {HIGH, LOW} = controller_eu ? _1607032_2_output : 8'bz;  // Controlled_Buffer controlled_buffer_5
  assign xor_1_out = _1607032_3_out0 ^ bit_extender_1_out;  // XOR_Gate xor_1, 8 bits wide
  assign bit_extender_1_out = {{7{controller_su}}, controller_su};  // Bit_Extender bit_extender_1
  Hex_Digit_Display hex_digit_display_1 (.value({out_11, out_10, out_9, out_8}));  // open: dp
  Hex_Digit_Display hex_digit_display_2 (.value({out_7, out_6, out_5, out_4}));  // open: dp
  Clock CLOCK (.out(CLOCK_out));
  not not_8 (not_8_out, controller_hlt);
  assign controlled_buffer_6_out = not_8_out ? CLOCK_out : 1'bz;  // Controlled_Buffer controlled_buffer_6

  // Notes on the sheet:
  //   1607098_Ashikur Rahaman
  //   1607032_Yamin  Arafat
  //   5+11-3=13
endmodule

// MAR
module MAR_4_bit__1607098 (
  input  Load,
  input  In0,
  input  In3,
  input  In2,
  input  In1,
  input  CP,
  input  CL,
  output Out1,
  output Out3,
  output Out2,
  output Out0
);

  wire and_1_out, and_2_out, and_3_out, and_4_out, and_5_out, and_6_out, and_7_out, and_8_out, not_1_out,
       or_1_out, or_2_out, or_3_out, or_4_out;

  and and_1 (and_1_out, Out3, not_1_out);
  or or_1 (or_1_out, and_1_out, and_2_out);
  and and_2 (and_2_out, In3, Load);
  D_Flip_Flop d_ff_1 (.clk(CP), .D(or_1_out), .Q(Out3), .en(1'b1), .reset(CL));  // open: Qn, preset
  and and_3 (and_3_out, Out2, not_1_out);
  or or_2 (or_2_out, and_3_out, and_4_out);
  and and_4 (and_4_out, In2, Load);
  D_Flip_Flop d_ff_2 (.clk(CP), .D(or_2_out), .Q(Out2), .en(1'b1), .reset(CL));  // open: Qn, preset
  and and_5 (and_5_out, Out1, not_1_out);
  and and_6 (and_6_out, In1, Load);
  or or_3 (or_3_out, and_5_out, and_6_out);
  D_Flip_Flop d_ff_3 (.clk(CP), .D(or_3_out), .Q(Out1), .en(1'b1), .reset(CL));  // open: Qn, preset
  and and_7 (and_7_out, Out0, not_1_out);
  and and_8 (and_8_out, In0, Load);
  or or_4 (or_4_out, and_7_out, and_8_out);
  D_Flip_Flop d_ff_4 (.clk(CP), .D(or_4_out), .Q(Out0), .en(1'b1), .reset(CL));  // open: Qn, preset
  not not_1 (not_1_out, Load);

  // Notes on the sheet:
  //   Ashikur Rahaman_1607098
endmodule

// A-Register
module A_Register_1607032 (
  input  Load,
  input  In3,
  input  In2,
  input  In1,
  input  In0,
  input  Clock,
  input  Clear,
  input  In7,
  input  In6,
  input  In5,
  input  In4,
  output Out0,
  output Out1,
  output Out2,
  output Out3,
  output Out7,
  output Out6,
  output Out5,
  output Out4
);

  MAR_4_bit__1607098 mar_4_bit_1607098_1 (
    .CP(Clock), .CL(Clear), .Load(Load), .In0(In0), .In1(In1), .In2(In2), .In3(In3), .Out0(Out0),
    .Out1(Out1), .Out2(Out2), .Out3(Out3));
  MAR_4_bit__1607098 mar_4_bit_1607098_2 (
    .CP(Clock), .CL(Clear), .Load(Load), .In0(In4), .In1(In5), .In2(In6), .In3(In7), .Out0(Out4),
    .Out1(Out5), .Out2(Out6), .Out3(Out7));

  // Notes on the sheet:
  //   1607032__Yamin_Arafat
endmodule

// PC
module program_counter_1607098___synchronous (
  input  Clock,
  input  Clear,
  output C3,
  output C2,
  output C1,
  output C0
);

  wire AND_2_out, AND_out;

  J_K_Flip_Flop _0 (.J(1'b1), .clk(Clock), .K(1'b1), .Q(C0), .reset(Clear));  // open: Qn, preset, en
  J_K_Flip_Flop _1 (.J(C0), .clk(Clock), .K(C0), .Q(C1), .reset(Clear));  // open: Qn, preset, en
  and AND (AND_out, C0, C1);
  and AND_2 (AND_2_out, C0, C1, C2);
  J_K_Flip_Flop _2 (.J(AND_out), .clk(Clock), .K(AND_out), .Q(C2), .reset(Clear));  // open: Qn, preset, en
  J_K_Flip_Flop _3 (.J(AND_2_out), .clk(Clock), .K(AND_2_out), .Q(C3), .reset(Clear));  // open: Qn, preset, en

  // Notes on the sheet:
  //   Ashikur Rahaman_1607098
endmodule

module Full_Adder_1607032 (
  input  A,
  input  B,
  input  Cin,
  output S,
  output Cout
);

  wire and_1_out, and_2_out, xor_1_out;

  xor xor_1 (xor_1_out, A, B);
  and and_1 (and_1_out, A, B);
  xor xor_2 (S, xor_1_out, Cin);
  and and_2 (and_2_out, xor_1_out, Cin);
  or or_1 (Cout, and_2_out, and_1_out);

  // Notes on the sheet:
  //   1607032_Yamin_Arafat
endmodule

// Add/Sub
module Adder_subtractor_1607032 (
  input  [7:0] A,
  input  Cin,
  input  [7:0] B,
  output [7:0] Output,
  output Cout
);

  wire FA0_cout, FA1_cout, FA2_cout, FA3_cout, FA4_cout, FA5_cout, FA6_cout;

  Full_Adder_1607032 FA0 (.A(A[0]), .B(B[0]), .Cin(Cin), .S(Output[0]), .Cout(FA0_cout));
  Full_Adder_1607032 FA1 (.A(A[1]), .B(B[1]), .Cin(FA0_cout), .S(Output[1]), .Cout(FA1_cout));
  Full_Adder_1607032 FA2 (.A(A[2]), .B(B[2]), .Cin(FA1_cout), .S(Output[2]), .Cout(FA2_cout));
  Full_Adder_1607032 FA3 (.A(A[3]), .B(B[3]), .Cin(FA2_cout), .S(Output[3]), .Cout(FA3_cout));
  Full_Adder_1607032 FA4 (.A(A[4]), .B(B[4]), .Cin(FA3_cout), .S(Output[4]), .Cout(FA4_cout));
  Full_Adder_1607032 FA5 (.A(A[5]), .B(B[5]), .Cin(FA4_cout), .S(Output[5]), .Cout(FA5_cout));
  Full_Adder_1607032 FA6 (.A(A[6]), .B(B[6]), .Cin(FA5_cout), .S(Output[6]), .Cout(FA6_cout));
  Full_Adder_1607032 FA7 (.A(A[7]), .B(B[7]), .Cin(FA6_cout), .S(Output[7]), .Cout(Cout));

  // Notes on the sheet:
  //   1607032_Yamin_Arafat
endmodule

// 1607032_1607098
module controller_1607032_1607098 (
  input  CLK,
  input  Clear,
  input  i7,
  input  i6,
  input  i5,
  input  i4,
  output Ep,
  output Cp,
  output nLm,
  output nCE,
  output nEl,
  output nLa,
  output Ea,
  output Eu,
  output nLb,
  output HLT,
  output nLl,
  output Su,
  output nLo
);

  wire c39_1607098_1__3, c39_1607098_1__6, c39_1607098_1__8, c39_1607098_1__11, c40_1607098_1__3,
       c40_1607098_1__6, c40_1607098_1__8, c40_1607098_1__11, c41_1607098_1__3, c41_1607098_1__6,
       c41_1607098_1__8, c41_1607098_1__11, c41_1607098_2__8, c41_1607098_2__11, c43_1607098_1__3,
       c43_1607098_1__6, c43_1607098_1__8, Instruction_decoder_add, Instruction_decoder_lda,
       Instruction_decoder_out, Instruction_decoder_sub, or_1_out, or_2_out, or_3_out, or_4_out, or_5_out,
       Ring_counter_t3, Ring_counter_t4, Ring_counter_t5, Ring_counter_t6;

  instruction_decode_1607032 Instruction_decoder (
    .i7(i7), .i6(i6), .i5(i5), .i4(i4), .LDA(Instruction_decoder_lda), .ADD(Instruction_decoder_add),
    .SUB(Instruction_decoder_sub), .OUT(Instruction_decoder_out), .HLT(HLT));
  ring_counter_1607098 Ring_counter (
    .Clock(CLK), .Clr(Clear), .T1(Ep), .T2(Cp), .T3(Ring_counter_t3), .T4(Ring_counter_t4),
    .T5(Ring_counter_t5), .T6(Ring_counter_t6));
  C39_1607098 c39_1607098_1 (
    ._1(Instruction_decoder_lda), ._4(Instruction_decoder_add), ._9(Instruction_decoder_sub),
    ._10(Ring_counter_t4), ._12(Instruction_decoder_lda), ._13(Ring_counter_t5), ._3(c39_1607098_1__3),
    ._6(c39_1607098_1__6), ._8(c39_1607098_1__8), ._11(c39_1607098_1__11));
  or or_1 (or_1_out, Ep, c39_1607098_1__3, c39_1607098_1__6, c39_1607098_1__8);
  not not_1 (nLm, or_1_out);
  C40_1607098 c40_1607098_1 (
    ._1(Instruction_decoder_add), ._4(Instruction_decoder_sub), ._5(Ring_counter_t5),
    ._9(Instruction_decoder_lda), ._12(Instruction_decoder_add), ._13(Ring_counter_t4),
    ._3(c40_1607098_1__3), ._6(c40_1607098_1__6), ._8(c40_1607098_1__8), ._11(c40_1607098_1__11));
  or or_2 (or_2_out, Ring_counter_t3, c39_1607098_1__11, c40_1607098_1__3, c40_1607098_1__6);
  not not_2 (nCE, or_2_out);
  C41_1607098 c41_1607098_1 (
    ._1(Instruction_decoder_sub), ._2(Ring_counter_t4), ._4(Instruction_decoder_lda), ._5(Ring_counter_t5),
    ._9(Instruction_decoder_add), ._12(Instruction_decoder_sub), ._13(Ring_counter_t6),
    ._3(c41_1607098_1__3), ._6(c41_1607098_1__6), ._8(c41_1607098_1__8), ._11(c41_1607098_1__11));
  or or_3 (or_3_out, c40_1607098_1__8, c40_1607098_1__11, c41_1607098_1__3);
  not not_3 (nEl, or_3_out);
  C41_1607098 c41_1607098_2 (
    ._1(Instruction_decoder_out), ._2(Ring_counter_t4), ._4(Instruction_decoder_sub), ._5(Ring_counter_t6),
    ._9(Instruction_decoder_add), ._12(Instruction_decoder_sub), ._13(Ring_counter_t6), ._3(Ea), ._6(Su),
    ._8(c41_1607098_2__8), ._11(c41_1607098_2__11));
  or or_4 (or_4_out, c41_1607098_1__6, c41_1607098_1__8, c41_1607098_1__11);
  not not_4 (nLa, or_4_out);
  C43_1607098 c43_1607098_1 (
    ._1(Instruction_decoder_add), ._4(Instruction_decoder_sub), ._5(Ring_counter_t5),
    ._9(Instruction_decoder_out), ._10(Ring_counter_t4), ._3(c43_1607098_1__3), ._6(c43_1607098_1__6),
    ._8(c43_1607098_1__8));
  or or_5 (or_5_out, c43_1607098_1__3, c43_1607098_1__6);
  or or_6 (Eu, c41_1607098_2__8, c41_1607098_2__11);
  not not_5 (nLb, or_5_out);
  not not_6 (nLo, c43_1607098_1__8);
  not not_7 (nLl, Ring_counter_t3);

  // Notes on the sheet:
  //   1607098_Ashikur Rahaman
  //   1607032__Yamin_Arafat
endmodule

// 1607098
module ring_counter_1607098 (
  input  Clock,
  input  Clr,
  output T1,
  output T2,
  output T3,
  output T4,
  output T5,
  output T6
);

  wire j_k_ff_1_qn, j_k_ff_2_qn, j_k_ff_3_qn, j_k_ff_4_qn, j_k_ff_5_qn, j_k_ff_6_qn;

  J_K_Flip_Flop j_k_ff_1 (
    .J(j_k_ff_6_qn), .clk(Clock), .K(T6), .Q(T1), .Qn(j_k_ff_1_qn), .reset(Clr));  // open: preset, en
  J_K_Flip_Flop j_k_ff_2 (
    .J(j_k_ff_1_qn), .clk(Clock), .K(T1), .Q(T2), .Qn(j_k_ff_2_qn), .reset(Clr));  // open: preset, en
  J_K_Flip_Flop j_k_ff_3 (
    .J(T2), .clk(Clock), .K(j_k_ff_2_qn), .Q(T3), .Qn(j_k_ff_3_qn), .reset(Clr));  // open: preset, en
  J_K_Flip_Flop j_k_ff_4 (
    .J(T3), .clk(Clock), .K(j_k_ff_3_qn), .Q(T4), .Qn(j_k_ff_4_qn), .reset(Clr));  // open: preset, en
  J_K_Flip_Flop j_k_ff_5 (
    .J(T4), .clk(Clock), .K(j_k_ff_4_qn), .Q(T5), .Qn(j_k_ff_5_qn), .reset(Clr));  // open: preset, en
  J_K_Flip_Flop j_k_ff_6 (
    .J(T5), .clk(Clock), .K(j_k_ff_5_qn), .Q(T6), .Qn(j_k_ff_6_qn), .reset(Clr));  // open: preset, en

  // Notes on the sheet:
  //   1607098_Ashikur Rahaman
endmodule

// 1607032
module instruction_decode_1607032 (
  input  i7,
  input  i6,
  input  i5,
  input  i4,
  output LDA,
  output ADD,
  output SUB,
  output OUT,
  output HLT
);

  wire not_1_out, not_2_out, not_3_out, not_4_out;

  not not_1 (not_1_out, i7);
  not not_2 (not_2_out, i5);
  not not_3 (not_3_out, i6);
  not not_4 (not_4_out, i4);
  and and_1 (LDA, not_1_out, not_3_out, not_2_out, not_4_out);
  and and_2 (ADD, not_1_out, not_3_out, not_2_out, i4);
  and and_3 (SUB, not_1_out, not_3_out, i5, not_4_out);
  and and_4 (OUT, i7, i6, i5, not_4_out);
  and and_5 (HLT, i7, i6, i5, i4);

  // Notes on the sheet:
  //   1607032__Yamin_Arafat
endmodule

// C39
module C39_1607098 (
  input  _1,
  input  _4,
  input  _9,
  input  _10,
  input  _12,
  input  _13,
  output _3,
  output _6,
  output _8,
  output _11
);

  and and_1 (_3, _1, _10);
  and and_2 (_6, _4, _10);
  and and_3 (_8, _9, _10);
  and and_4 (_11, _12, _13);

  // Notes on the sheet:
  //   1607098_Ashikur Rahaman
endmodule

// C40
module C40_1607098 (
  input  _1,
  input  _4,
  input  _5,
  input  _9,
  input  _12,
  input  _13,
  output _3,
  output _6,
  output _8,
  output _11
);

  and and_1 (_3, _1, _5);
  and and_2 (_8, _9, _13);
  and and_3 (_6, _4, _5);
  and and_4 (_11, _12, _13);

  // Notes on the sheet:
  //   1607098_Ashikur Rahaman
endmodule

// C41
module C41_1607098 (
  input  _1,
  input  _2,
  input  _4,
  input  _5,
  input  _9,
  input  _12,
  input  _13,
  output _3,
  output _6,
  output _8,
  output _11
);

  and and_1 (_3, _1, _2);
  and and_2 (_6, _4, _5);
  and and_3 (_11, _12, _13);
  and and_4 (_8, _9, _13);

  // Notes on the sheet:
  //   1607098_Ashikur Rahaman
endmodule

// C43
module C43_1607098 (
  input  _1,
  input  _4,
  input  _5,
  input  _9,
  input  _10,
  output _3,
  output _6,
  output _8
);

  and and_1 (_3, _1, _5);
  and and_2 (_8, _9, _10);
  and and_3 (_6, _4, _5);

  // Notes on the sheet:
  //   1607098_Ashikur Rahaman
endmodule

// B-Register
module B_Register_1607032 (
  input  Load,
  input  In3,
  input  In2,
  input  In1,
  input  In0,
  input  Clock,
  input  Clear,
  input  In7,
  input  In6,
  input  In5,
  input  In4,
  output Out0,
  output Out1,
  output Out2,
  output Out3,
  output Out7,
  output Out6,
  output Out5,
  output Out4
);

  MAR_4_bit__1607098 mar_4_bit_1607098_1 (
    .CP(Clock), .CL(Clear), .Load(Load), .In0(In0), .In1(In1), .In2(In2), .In3(In3), .Out0(Out0),
    .Out1(Out1), .Out2(Out2), .Out3(Out3));
  MAR_4_bit__1607098 mar_4_bit_1607098_2 (
    .CP(Clock), .CL(Clear), .Load(Load), .In0(In4), .In1(In5), .In2(In6), .In3(In7), .Out0(Out4),
    .Out1(Out5), .Out2(Out6), .Out3(Out7));

  // Notes on the sheet:
  //   1607032__Yamin_Arafat
endmodule

// Output-Register
module Output_Register_1607032 (
  input  Load,
  input  In3,
  input  In2,
  input  In1,
  input  In0,
  input  Clock,
  input  Clear,
  input  In7,
  input  In6,
  input  In5,
  input  In4,
  output [7:0] out_12
);

  MAR_4_bit__1607098 mar_4_bit_1607098_1 (
    .CP(Clock), .CL(Clear), .Load(Load), .In0(In0), .In1(In1), .In2(In2), .In3(In3), .Out0(out_12[0]),
    .Out1(out_12[1]), .Out2(out_12[2]), .Out3(out_12[3]));
  MAR_4_bit__1607098 mar_4_bit_1607098_2 (
    .CP(Clock), .CL(Clear), .Load(Load), .In0(In4), .In1(In5), .In2(In6), .In3(In7), .Out0(out_12[4]),
    .Out1(out_12[5]), .Out2(out_12[6]), .Out3(out_12[7]));

  // Notes on the sheet:
  //   1607032__Yamin_Arafat
endmodule

// Instruction-Register
module Instruction_Registe_1607098 (
  input  Load,
  input  In3,
  input  In2,
  input  In1,
  input  In0,
  input  Clock,
  input  Clear,
  input  In7,
  input  In6,
  input  In5,
  input  In4,
  output Out0,
  output Out1,
  output Out2,
  output Out3,
  output Out7,
  output Out6,
  output Out5,
  output Out4
);

  MAR_4_bit__1607098 mar_4_bit_1607098_1 (
    .CP(Clock), .CL(Clear), .Load(Load), .In0(In0), .In1(In1), .In2(In2), .In3(In3), .Out0(Out0),
    .Out1(Out1), .Out2(Out2), .Out3(Out3));
  MAR_4_bit__1607098 mar_4_bit_1607098_2 (
    .CP(Clock), .CL(Clear), .Load(Load), .In0(In4), .In1(In5), .In2(In6), .In3(In7), .Out0(Out4),
    .Out1(Out5), .Out2(Out6), .Out3(Out7));

  // Notes on the sheet:
  //   Ashikur Rahaman_1607098
endmodule
